// Logisim project td1.circ as structural Verilog: 3 circuits, main circuit test
module test (
  input  [7:0] in_1,
  input  [1:0] in_2,
  input  in_3,
  input  [1:0] in_4,
  input  [1:0] in_5,
  input  in_6,
  output [7:0] out_7,
  output [7:0] out_8
);

  wire clock_1_out;

  Clock clock_1 (.out(clock_1_out));
  // Probe on out_7
  reg8_bank reg8_bank_1 (
    .rd_data_i(in_1), .rs1_add_i(in_2), .we_i(in_3), .clk_i(clock_1_out), .rs2_add_i(in_4), .rd_add_i(in_5),
    .rst_i(in_6), .rs1_data_o(out_7), .rs2_data_o(out_8));
  // Probe on out_8
endmodule

module alu (
  input  [31:0] op1_i,
  input  [31:0] op2_i,
  input  [3:0] func_i,
  output [31:0] d_o,
  output zero_o,
  output lt_o
);

  wire comparator_1_eq, comparator_1_gt, comparator_2_eq, comparator_2_gt;
  wire [0:0] comparator_1_lt, comparator_2_lt;
  wire [31:0] adder_1_out, and_1_out, or_1_out, shifter_1_out, shifter_2_out, shifter_3_out,
       subtractor_1_out, xor_1_out;

  Adder #(.width(32)) adder_1 (.a(op1_i), .b(op2_i), .out(adder_1_out), .cin(1'b0));  // open: cout
  Subtractor #(.width(32)) subtractor_1 (.a(op1_i), .b(op2_i), .out(subtractor_1_out), .bin(1'b0));  // open: bout
  Shifter #(.width(32)) shifter_1 (.in(op1_i), .\dist (op2_i[4:0]), .out(shifter_1_out));
  Shifter #(.shift("lr"), .width(32)) shifter_2 (.in(op1_i), .\dist (op2_i[4:0]), .out(shifter_2_out));
  Shifter #(.shift("ar"), .width(32)) shifter_3 (.in(op1_i), .\dist (op2_i[4:0]), .out(shifter_3_out));
  Comparator #(.width(32)) comparator_1 (
    .a(op1_i), .b(op2_i), .gt(comparator_1_gt), .eq(comparator_1_eq), .lt(comparator_1_lt[0]));
  Comparator #(.mode("unsigned"), .width(32)) comparator_2 (
    .a(op1_i), .b(op2_i), .gt(comparator_2_gt), .eq(comparator_2_eq), .lt(comparator_2_lt[0]));
  assign and_1_out = op1_i & op2_i;  // AND_Gate and_1, 32 bits wide
  assign or_1_out = op1_i | op2_i;  // OR_Gate or_1, 32 bits wide
  assign xor_1_out = op1_i ^ op2_i;  // XOR_Gate xor_1, 32 bits wide
  // NoConnect on comparator_1_gt
  // NoConnect on comparator_1_eq
  // NoConnect on comparator_2_gt
  // NoConnect on comparator_2_eq
  Multiplexer #(.select(4), .width(32)) multiplexer_1 (
    .in0({32{1'b0}}), .in1(adder_1_out), .in2(subtractor_1_out), .in3(shifter_1_out), .in4(shifter_2_out),
    .in5(shifter_3_out), .in6(and_1_out), .in7(or_1_out), .in8(xor_1_out),
    .in9({{31{1'b0}}, comparator_1_lt[0]}), .in10({{31{1'b0}}, comparator_2_lt[0]}), .in11({32{1'b0}}),
    .in12({32{1'b0}}), .in13({32{1'b0}}), .in14({32{1'b0}}), .in15({32{1'b0}}), .out(d_o), .sel(func_i));
  Comparator #(.width(32)) comparator_3 (.a(d_o), .b({32{1'b0}}), .eq(zero_o), .lt(lt_o));  // open: gt
endmodule

module reg8_bank (
  input  [7:0] rd_data_i,
  input  [1:0] rs1_add_i,
  input  we_i,
  input  clk_i,
  input  [1:0] rs2_add_i,
  input  [1:0] rd_add_i,
  input  rst_i,
  output [7:0] rs1_data_o,
  output [7:0] rs2_data_o
);

  wire demultiplexer_1_out0, demultiplexer_1_out1, demultiplexer_1_out2, demultiplexer_1_out3;
  wire [7:0] register_1_q, register_2_q, register_3_q, register_4_q;

  Demultiplexer #(.select(2)) demultiplexer_1 (
    .out0(demultiplexer_1_out0), .out1(demultiplexer_1_out1), .out2(demultiplexer_1_out2),
    .out3(demultiplexer_1_out3), .in(we_i), .sel(rd_add_i));
  Register register_1 (.D(rd_data_i), .en(demultiplexer_1_out0), .clk(clk_i), .Q(register_1_q), .clr(rst_i));
  Register register_2 (.D(rd_data_i), .en(demultiplexer_1_out1), .clk(clk_i), .Q(register_2_q), .clr(rst_i));
  Register register_3 (.D(rd_data_i), .en(demultiplexer_1_out2), .clk(clk_i), .Q(register_3_q), .clr(rst_i));
  Register register_4 (.D(rd_data_i), .en(demultiplexer_1_out3), .clk(clk_i), .Q(register_4_q), .clr(rst_i));
  Multiplexer #(.select(2), .width(8)) multiplexer_1 (
    .in0(register_1_q), .in1(register_2_q), .in2(register_3_q), .in3(register_4_q), .out(rs1_data_o),
    .sel(rs1_add_i));
  Multiplexer #(.select(2), .width(8)) multiplexer_2 (
    .in0(register_1_q), .in1(register_2_q), .in2(register_3_q), .in3(register_4_q), .out(rs2_data_o),
    .sel(rs2_add_i));
endmodule
