// Logisim project riscv_monocycle_incomplete.circ as structural Verilog: 7 circuits, main circuit monocycle
module data_path (
  input  alu_src1_i,
  input  [3:0] alu_control_i,
  input  alu_src2_i,
  input  reg_write_i,
  input  clk_i,
  input  [1:0] imm_gen_sel_i,
  input  rst_i,
  output [31:0] instruction_o,
  output zero_o,
  output it_o
);

  wire [7:0] adder_1_out, register_1_q;
  wire [31:0] alu_1_d_o, imm_gen_1_imm_o, multiplexer_1_out, multiplexer_2_out, registers_bank_1_rs1_data_o,
       registers_bank_1_rs2_data_o;

  Adder adder_1 (.a(register_1_q), .b(8'h4), .out(adder_1_out), .cin(1'b0));  // open: cout
  // Probe on register_1_q
  Register register_1 (.D(adder_1_out), .en(1'b1), .clk(clk_i), .Q(register_1_q), .clr(rst_i));
  memory memory_1 (
    .we_i(1'b0), .re_i(1'b1), .clk_i(clk_i), .add_i(register_1_q), .d_i({32{1'b0}}), .d_o(instruction_o));
  registers_bank registers_bank_1 (
    .clk_i(clk_i), .rst_i(rst_i), .rd_data_i(alu_1_d_o), .rs1_data_i(instruction_o[19:15]),
    .rs2_data_i(instruction_o[24:20]), .rd_add(instruction_o[11:7]), .we_i(reg_write_i),
    .rs1_data_o(registers_bank_1_rs1_data_o), .rs2_data_o(registers_bank_1_rs2_data_o));
  Imm_Gen imm_gen_1 (.Imm_i(instruction_o), .imm_gen_sel_i(imm_gen_sel_i), .Imm_o(imm_gen_1_imm_o));
  // Probe on multiplexer_1_out
  Multiplexer #(.width(32)) multiplexer_1 (
    .in0(registers_bank_1_rs1_data_o), .in1(imm_gen_1_imm_o), .out(multiplexer_1_out), .sel(alu_src1_i));
  Multiplexer #(.width(32)) multiplexer_2 (
    .in0(registers_bank_1_rs2_data_o), .in1(imm_gen_1_imm_o), .out(multiplexer_2_out), .sel(alu_src2_i));
  // Probe on multiplexer_2_out
  // Probe on alu_1_d_o
  alu alu_1 (
    .op1_i(multiplexer_1_out), .op2_i(multiplexer_2_out), .func_i(alu_control_i), .d_o(alu_1_d_o),
    .zero_o(zero_o), .lt_o(it_o));

  // Notes on the sheet:
  //   Placer le banc de registres 32 bits  ici :
endmodule

module test (
  input  in_1,
  input  [31:0] in_2,
  input  [4:0] in_3,
  input  [4:0] in_4,
  input  [4:0] in_5,
  input  in_6
);

  wire clock_1_out;
  wire [31:0] registers_bank_1_rs1_data_o, registers_bank_1_rs2_data_o;

  Clock clock_1 (.out(clock_1_out));
  registers_bank registers_bank_1 (
    .clk_i(clock_1_out), .rst_i(in_1), .rd_data_i(in_2), .rs1_data_i(in_3), .rs2_data_i(in_4), .rd_add(in_5),
    .we_i(in_6), .rs1_data_o(registers_bank_1_rs1_data_o), .rs2_data_o(registers_bank_1_rs2_data_o));
  // Probe on registers_bank_1_rs1_data_o
  // Probe on registers_bank_1_rs2_data_o

  // Notes on the sheet:
  //   Placer le banc de registres 32 bits  ici :
endmodule

module alu (
  input  [31:0] op1_i,
  input  [31:0] op2_i,
  input  [3:0] func_i,
  output [31:0] d_o,
  output zero_o,
  output lt_o
);

  wire comparator_1_eq, comparator_1_gt, comparator_2_eq, comparator_2_gt;
  wire [0:0] comparator_1_lt, comparator_2_lt;
  wire [31:0] adder_1_out, and_1_out, or_1_out, shifter_1_out, shifter_2_out, shifter_3_out,
       subtractor_1_out, xor_1_out;

  Adder #(.width(32)) adder_1 (.a(op1_i), .b(op2_i), .out(adder_1_out), .cin(1'b0));  // open: cout
  Subtractor #(.width(32)) subtractor_1 (.a(op1_i), .b(op2_i), .out(subtractor_1_out), .bin(1'b0));  // open: bout
  Shifter #(.width(32)) shifter_1 (.in(op1_i), .\dist (op2_i[4:0]), .out(shifter_1_out));
  Shifter #(.shift("lr"), .width(32)) shifter_2 (.in(op1_i), .\dist (op2_i[4:0]), .out(shifter_2_out));
  Shifter #(.shift("ar"), .width(32)) shifter_3 (.in(op1_i), .\dist (op2_i[4:0]), .out(shifter_3_out));
  Comparator #(.width(32)) comparator_1 (
    .a(op1_i), .b(op2_i), .gt(comparator_1_gt), .eq(comparator_1_eq), .lt(comparator_1_lt[0]));
  Comparator #(.mode("unsigned"), .width(32)) comparator_2 (
    .a(op1_i), .b(op2_i), .gt(comparator_2_gt), .eq(comparator_2_eq), .lt(comparator_2_lt[0]));
  assign and_1_out = op1_i & op2_i;  // AND_Gate and_1, 32 bits wide
  assign or_1_out = op1_i | op2_i;  // OR_Gate or_1, 32 bits wide
  assign xor_1_out = op1_i ^ op2_i;  // XOR_Gate xor_1, 32 bits wide
  // NoConnect on comparator_1_gt
  // NoConnect on comparator_1_eq
  // NoConnect on comparator_2_gt
  // NoConnect on comparator_2_eq
  Multiplexer #(.select(4), .width(32)) multiplexer_1 (
    .in0({32{1'b0}}), .in1(adder_1_out), .in2(subtractor_1_out), .in3(shifter_1_out), .in4(shifter_2_out),
    .in5(shifter_3_out), .in6(and_1_out), .in7(or_1_out), .in8(xor_1_out),
    .in9({{31{1'b0}}, comparator_1_lt[0]}), .in10({{31{1'b0}}, comparator_2_lt[0]}), .in11(op1_i),
    .in12({32{1'b0}}), .in13({32{1'b0}}), .in14({32{1'b0}}), .in15({32{1'b0}}), .out(d_o), .sel(func_i));
  Comparator #(.width(32)) comparator_3 (.a(d_o), .b({32{1'b0}}), .eq(zero_o), .lt(lt_o));  // open: gt
endmodule

module memory (
  input  we_i,
  input  re_i,
  input  clk_i,
  input  [7:0] add_i,
  input  [31:0] d_i,
  output [31:0] d_o
);

  RAM #(.asyncread("true")) ram_1 (
    .addr({2'b00, add_i[7:2]}), .we(we_i), .oe(re_i), .clk(clk_i), .din(d_i[7:0]), .dout(d_o[7:0]));
  RAM #(.asyncread("true")) ram_2 (
    .addr({2'b00, add_i[7:2]}), .we(we_i), .oe(re_i), .clk(clk_i), .din(d_i[15:8]), .dout(d_o[15:8]));
  RAM #(.asyncread("true")) ram_3 (
    .addr({2'b00, add_i[7:2]}), .we(we_i), .oe(re_i), .clk(clk_i), .din(d_i[23:16]), .dout(d_o[23:16]));
  RAM #(.asyncread("true")) ram_4 (
    .addr({2'b00, add_i[7:2]}), .we(we_i), .oe(re_i), .clk(clk_i), .din(d_i[31:24]), .dout(d_o[31:24]));

  // Notes on the sheet:
  //   BL0
  //   BL1
  //   BL2
  //   BL3
endmodule

module control_path (
  input  [31:0] instruction_i,
  input  alu_zero_i,
  input  alu_lt_i,
  output [3:0] alu_control_o,
  output reg_write_o,
  output alu_src1_o,
  output alu_src2_o,
  output [1:0] imm_gen_sel_o
);

  wire comparator_1_eq, comparator_2_eq, comparator_3_eq;
  wire [2:0] priority_encoder_1_out;
  wire [3:0] I_Type_func_out, R_Type_func_out;

  Comparator #(.width(5)) comparator_1 (.a(5'b01100), .b(instruction_i[6:2]), .eq(comparator_1_eq));  // open: gt, lt
  Comparator #(.width(5)) comparator_2 (.a(5'b00100), .b(instruction_i[6:2]), .eq(comparator_2_eq));  // open: gt, lt
  Comparator #(.width(5)) comparator_3 (.a(5'b01101), .b(instruction_i[6:2]), .eq(comparator_3_eq));  // open: gt, lt
  PLA #(.in_width(3), .out_width(4), .\table ("000 0001 # add\n110 0111 # or")) R_Type_func (
    .in(instruction_i[14:12]), .out(R_Type_func_out));
  PLA #(.in_width(3), .out_width(4), .\table ("000 0001 # addi")) I_Type_func (
    .in(instruction_i[14:12]), .out(I_Type_func_out));
  Priority_Encoder priority_encoder_1 (
    .in0(comparator_1_eq), .in1(comparator_2_eq), .in2(comparator_3_eq), .out(priority_encoder_1_out),
    .en_in(1'b1));  // open: in3, in4, in5, in6, in7, gs, en_out
  // Probe on priority_encoder_1_out
  Multiplexer #(.select(3), .width(4)) multiplexer_1 (
    .in0(R_Type_func_out), .in1(I_Type_func_out), .out(alu_control_o), .sel(priority_encoder_1_out));  // open: in2, in3, in4, in5, in6, in7
  Multiplexer #(.select(3)) multiplexer_2 (
    .in0(1'b1), .in1(1'b1), .in2(1'b1), .out(reg_write_o), .sel(priority_encoder_1_out));  // open: in3, in4, in5, in6, in7
  Multiplexer #(.select(3)) multiplexer_3 (
    .in0(1'b0), .in1(1'b0), .in2(1'b1), .out(alu_src1_o), .sel(priority_encoder_1_out));  // open: in3, in4, in5, in6, in7
  Multiplexer #(.select(3)) multiplexer_4 (
    .in0(1'b0), .in1(1'b1), .in2(1'b1), .out(alu_src2_o), .sel(priority_encoder_1_out));  // open: in3, in4, in5, in6, in7
  Multiplexer #(.select(3), .width(2)) multiplexer_5 (
    .in0(2'b00), .in1(2'b00), .in2(2'b01), .out(imm_gen_sel_o), .sel(priority_encoder_1_out));  // open: in3, in4, in5, in6, in7

  // Notes on the sheet:
  //   instruction_i: initial=0x1
  //   opcode
  //   func_3
  //   func_7
  //   I_TYPE
  //   U_TYPE
  //   R_TYPE
  //   R_TYPE
  //   R_TYPE
endmodule

module monocycle (
  input  rst
);

  wire clk_out, control_path_1_alu_src1_o, control_path_1_alu_src2_o, control_path_1_reg_write_o,
       data_path_1_it_o, data_path_1_zero_o;
  wire [1:0] control_path_1_imm_gen_sel_o;
  wire [3:0] control_path_1_alu_control_o;
  wire [31:0] data_path_1_instruction_o;

  Clock clk (.out(clk_out));
  data_path data_path_1 (
    .alu_src1_i(control_path_1_alu_src1_o), .alu_control_i(control_path_1_alu_control_o),
    .alu_src2_i(control_path_1_alu_src2_o), .reg_write_i(control_path_1_reg_write_o), .clk_i(clk_out),
    .imm_gen_sel_i(control_path_1_imm_gen_sel_o), .rst_i(rst), .instruction_o(data_path_1_instruction_o),
    .zero_o(data_path_1_zero_o), .it_o(data_path_1_it_o));
  control_path control_path_1 (
    .instruction_i(data_path_1_instruction_o), .alu_zero_i(data_path_1_zero_o), .alu_lt_i(data_path_1_it_o),
    .alu_control_o(control_path_1_alu_control_o), .reg_write_o(control_path_1_reg_write_o),
    .alu_src1_o(control_path_1_alu_src1_o), .alu_src2_o(control_path_1_alu_src2_o),
    .imm_gen_sel_o(control_path_1_imm_gen_sel_o));

  // Notes on the sheet:
  //   rst: pull=down
endmodule

module Imm_Gen (
  input  [31:0] Imm_i,
  input  [1:0] imm_gen_sel_i,
  output [31:0] Imm_o
);

  wire [11:0] demultiplexer_1_out0_2, demultiplexer_1_out1;
  wire [19:0] demultiplexer_1_out0, demultiplexer_1_out1_2;
  wire [20:0] multiplexer_1_out;

  Demultiplexer #(.select(2), .width(32)) demultiplexer_1 (
    .out0({demultiplexer_1_out0_2, demultiplexer_1_out0}),
    .out1({demultiplexer_1_out1_2, demultiplexer_1_out1}), .in(Imm_i), .sel(imm_gen_sel_i));  // open: out2, out3
  Multiplexer #(.width(21)) multiplexer_1 (
    .in0({21{1'b0}}), .in1({21{1'b1}}), .out(multiplexer_1_out), .sel(demultiplexer_1_out0_2[11]));
  Multiplexer #(.select(2), .width(32)) multiplexer_2 (
    .in0({multiplexer_1_out, demultiplexer_1_out0_2[10:0]}), .in1({demultiplexer_1_out1_2, {12{1'b0}}}),
    .out(Imm_o), .sel(imm_gen_sel_i));  // open: in2, in3
endmodule
