// Logisim project immediate_generator.circ as structural Verilog: 1 circuit, main circuit imm_gen
module imm_gen (
  input  [31:0] Imm_i,
  input  [1:0] imm_gen_sel_i,
  output [31:0] Imm_o
);

  wire [11:0] demultiplexer_1_out0_2, demultiplexer_1_out1;
  wire [19:0] demultiplexer_1_out0, demultiplexer_1_out1_2;
  wire [20:0] multiplexer_1_out;

  Demultiplexer #(.select(2), .width(32)) demultiplexer_1 (
    .out0({demultiplexer_1_out0_2, demultiplexer_1_out0}),
    .out1({demultiplexer_1_out1_2, demultiplexer_1_out1}), .in(Imm_i), .sel(imm_gen_sel_i));  // open: out2, out3
  Multiplexer #(.width(21)) multiplexer_1 (
    .in0({21{1'b0}}), .in1({21{1'b1}}), .out(multiplexer_1_out), .sel(demultiplexer_1_out0_2[11]));
  Multiplexer #(.select(2), .width(32)) multiplexer_2 (
    .in0({multiplexer_1_out, demultiplexer_1_out0_2[10:0]}), .in1({demultiplexer_1_out1_2, {12{1'b0}}}),
    .out(Imm_o), .sel(imm_gen_sel_i));  // open: in2, in3
endmodule
