// Logisim project riscv_5_stages_incomplete.circ as structural Verilog: 7 circuits, main circuit test
module data_path (
  input  [3:0] alu_control_i,
  input  alu_src1_i,
  input  mem_we_i,
  input  stall_i,
  input  wb_sel_i,
  input  [4:0] rd_add_i,
  input  reg_write_i,
  input  [1:0] imm_gen_sel_i,
  input  alu_src2_i,
  input  clk_i,
  input  rst_i,
  output [31:0] instruction_o,
  output zero_o,
  output it_o
);

  wire clk_i_t, not_1_out;
  wire [7:0] adder_1_out, register_1_q;
  wire [31:0] alu_1_d_o, data_d_o, DEC_DP_q, EXE_OP1_IMM_DP_q, EXE_OP2_DP_q, EXE_OP2_IMM_DP_q,
       imm_gen_1_imm_o, MEM_ALUO_DP_q, MEM_OP2_DP_q, multiplexer_1_out, multiplexer_2_out, multiplexer_3_out,
       register_bank_1_rs1_data_o, register_bank_1_rs2_data_o, WB_ALUO_DP_q, WB_MEMO_DP_q;

  not not_1 (not_1_out, stall_i);
  // Probe on register_1_q
  Adder adder_1 (.a(register_1_q), .b(8'h4), .out(adder_1_out), .cin(1'b0));  // open: cout
  Register register_1 (.D(adder_1_out), .en(not_1_out), .clk(clk_i), .Q(register_1_q), .clr(rst_i));
  Register #(.width(32)) DEC_DP (.D(instruction_o), .en(not_1_out), .clk(clk_i), .Q(DEC_DP_q), .clr(rst_i));
  instruction_memory instruction_memory_1 (.add_i(register_1_q), .data_o(instruction_o));
  // Probe on register_bank_1_rs1_data_o
  register_bank register_bank_1 (
    .clk_i(clk_i), .rs1_add_i(DEC_DP_q[19:15]), .rd_data_i(multiplexer_3_out), .rs2_add_i(DEC_DP_q[24:20]),
    .rd_add_i(rd_add_i), .we_i(reg_write_i), .rst_i(rst_i), .rs1_data_o(register_bank_1_rs1_data_o),
    .rs2_data_o(register_bank_1_rs2_data_o));
  // Probe on register_bank_1_rs2_data_o
  imm_gen imm_gen_1 (.Imm_i(DEC_DP_q), .imm_gen_sel_i(imm_gen_sel_i), .Imm_o(imm_gen_1_imm_o));
  // Probe on multiplexer_3_out
  Multiplexer #(.width(32)) multiplexer_1 (
    .in0(register_bank_1_rs1_data_o), .in1(imm_gen_1_imm_o), .out(multiplexer_1_out), .sel(alu_src1_i));
  // Probe on multiplexer_2_out
  Multiplexer #(.width(32)) multiplexer_2 (
    .in0(register_bank_1_rs2_data_o), .in1(imm_gen_1_imm_o), .out(multiplexer_2_out), .sel(alu_src2_i));
  Register #(.width(32)) EXE_OP1_IMM_DP (
    .D(multiplexer_1_out), .en(1'b1), .clk(clk_i), .Q(EXE_OP1_IMM_DP_q), .clr(rst_i));
  Register #(.width(32)) EXE_OP2_DP (
    .D(register_bank_1_rs2_data_o), .en(1'b1), .clk(clk_i), .Q(EXE_OP2_DP_q), .clr(rst_i));
  Register #(.width(32)) EXE_OP2_IMM_DP (
    .D(multiplexer_2_out), .en(1'b1), .clk(clk_i), .Q(EXE_OP2_IMM_DP_q), .clr(rst_i));
  // Probe on EXE_OP1_IMM_DP_q
  // Probe on EXE_OP2_IMM_DP_q
  // Probe on alu_1_d_o
  alu alu_1 (
    .op1_i(EXE_OP1_IMM_DP_q), .op2_i(EXE_OP2_IMM_DP_q), .func_i(alu_control_i), .d_o(alu_1_d_o),
    .zero_o(zero_o), .lt_o(it_o));
  Register #(.width(32)) MEM_ALUO_DP (.D(alu_1_d_o), .en(1'b1), .clk(clk_i), .Q(MEM_ALUO_DP_q), .clr(rst_i));
  Register #(.width(32)) MEM_OP2_DP (.D(EXE_OP2_DP_q), .en(1'b1), .clk(clk_i), .Q(MEM_OP2_DP_q), .clr(rst_i));
  Register #(.width(32)) WB_MEMO_DP (.D(data_d_o), .en(1'b1), .clk(clk_i), .Q(WB_MEMO_DP_q), .clr(rst_i));
  data_memory data (
    .we_i(mem_we_i), .re_i(1'b1), .clk_i(clk_i_t), .add_i(MEM_ALUO_DP_q[7:0]), .d_i(MEM_OP2_DP_q),
    .d_o(data_d_o));
  Register #(.width(32)) WB_ALUO_DP (.D(MEM_ALUO_DP_q), .en(1'b1), .clk(clk_i), .Q(WB_ALUO_DP_q), .clr(rst_i));
  Multiplexer #(.width(32)) multiplexer_3 (
    .in0(WB_MEMO_DP_q), .in1(WB_ALUO_DP_q), .out(multiplexer_3_out), .sel(wb_sel_i));

  // Notes on the sheet:
  //   IF
  //   Placer le banc de registres 32 bits  ici :
  //   Placer le générateur de valeur imm ici :
  //   ID
  //   EXE
  //   MEM
  //   WB
endmodule

module test (
  input  rst
);

  wire clk_out;

  Clock clk (.out(clk_out));
  pipeline_5stages pipeline_5stages_1 (.clk_i(clk_out), .rst_i(rst));
endmodule

module alu (
  input  [31:0] op1_i,
  input  [31:0] op2_i,
  input  [3:0] func_i,
  output [31:0] d_o,
  output zero_o,
  output lt_o
);

  wire comparator_1_eq, comparator_1_gt, comparator_2_eq, comparator_2_gt;
  wire [0:0] comparator_1_lt, comparator_2_lt;
  wire [31:0] adder_1_out, and_1_out, or_1_out, shifter_1_out, shifter_2_out, shifter_3_out,
       subtractor_1_out, xor_1_out;

  Adder #(.width(32)) adder_1 (.a(op1_i), .b(op2_i), .out(adder_1_out), .cin(1'b0));  // open: cout
  Subtractor #(.width(32)) subtractor_1 (.a(op1_i), .b(op2_i), .out(subtractor_1_out), .bin(1'b0));  // open: bout
  Shifter #(.width(32)) shifter_1 (.in(op1_i), .\dist (op2_i[4:0]), .out(shifter_1_out));
  Shifter #(.shift("lr"), .width(32)) shifter_2 (.in(op1_i), .\dist (op2_i[4:0]), .out(shifter_2_out));
  Shifter #(.shift("ar"), .width(32)) shifter_3 (.in(op1_i), .\dist (op2_i[4:0]), .out(shifter_3_out));
  Comparator #(.width(32)) comparator_1 (
    .a(op1_i), .b(op2_i), .gt(comparator_1_gt), .eq(comparator_1_eq), .lt(comparator_1_lt[0]));
  Comparator #(.mode("unsigned"), .width(32)) comparator_2 (
    .a(op1_i), .b(op2_i), .gt(comparator_2_gt), .eq(comparator_2_eq), .lt(comparator_2_lt[0]));
  assign and_1_out = op1_i & op2_i;  // AND_Gate and_1, 32 bits wide
  assign or_1_out = op1_i | op2_i;  // OR_Gate or_1, 32 bits wide
  assign xor_1_out = op1_i ^ op2_i;  // XOR_Gate xor_1, 32 bits wide
  // NoConnect on comparator_1_gt
  // NoConnect on comparator_1_eq
  // NoConnect on comparator_2_gt
  // NoConnect on comparator_2_eq
  Multiplexer #(.select(4), .width(32)) multiplexer_1 (
    .in0({32{1'b0}}), .in1(adder_1_out), .in2(subtractor_1_out), .in3(shifter_1_out), .in4(shifter_2_out),
    .in5(shifter_3_out), .in6(and_1_out), .in7(or_1_out), .in8(xor_1_out),
    .in9({{31{1'b0}}, comparator_1_lt[0]}), .in10({{31{1'b0}}, comparator_2_lt[0]}), .in11(op1_i),
    .in12({32{1'b0}}), .in13({32{1'b0}}), .in14({32{1'b0}}), .in15({32{1'b0}}), .out(d_o), .sel(func_i));
  Comparator #(.width(32)) comparator_3 (.a(d_o), .b({32{1'b0}}), .eq(zero_o), .lt(lt_o));  // open: gt
endmodule

module data_memory (
  input  we_i,
  input  re_i,
  input  clk_i,
  input  [7:0] add_i,
  input  [31:0] d_i,
  output [31:0] d_o
);

  RAM #(.asyncread("true")) ram_1 (
    .addr({2'b00, add_i[7:2]}), .we(we_i), .oe(re_i), .clk(clk_i), .din(d_i[7:0]), .dout(d_o[7:0]));
  RAM #(.asyncread("true")) ram_2 (
    .addr({2'b00, add_i[7:2]}), .we(we_i), .oe(re_i), .clk(clk_i), .din(d_i[15:8]), .dout(d_o[15:8]));
  RAM #(.asyncread("true")) ram_3 (
    .addr({2'b00, add_i[7:2]}), .we(we_i), .oe(re_i), .clk(clk_i), .din(d_i[23:16]), .dout(d_o[23:16]));
  RAM #(.asyncread("true")) ram_4 (
    .addr({2'b00, add_i[7:2]}), .we(we_i), .oe(re_i), .clk(clk_i), .din(d_i[31:24]), .dout(d_o[31:24]));

  // Notes on the sheet:
  //   BL0
  //   BL1
  //   BL2
  //   BL3
endmodule

module control_path (
  input  [31:0] instruction_i,
  input  clk_i,
  input  rst_i,
  input  alu_zero_i,
  input  alu_lt_i,
  output [1:0] imm_gen_sel_o,
  output alu_src2_o,
  output alu_src1_o,
  output [3:0] alu_control_o,
  output mem_we_o,
  output [4:0] rd_add_o,
  output wb_sel_o,
  output stall_o,
  output reg_write_o
);

  wire comparator_1_eq, comparator_2_eq, comparator_3_eq, comparator_4_eq, comparator_5_eq, comparator_6_eq,
       not_1_out, or_1_out;
  wire [2:0] EXE_CP_q_2, EXE_OP_q, MEM_OP_q, multiplexer_2_out, priority_encoder_1_out, WB_OP_q;
  wire [3:0] R_Type_func_out;
  wire [4:0] rs1_add_w, rs2_add_w;
  wire [6:0] EXE_CP_q_3;
  wire [24:0] EXE_CP_q;
  wire [31:0] DEC_CP_q, MEM_CP_q, multiplexer_1_out, WB_CP_q;

  // Probe on MEM_CP_q
  // Probe on instruction_i
  not not_1 (not_1_out, stall_o);
  // Probe on {DEC_CP_q[31:25], rs2_add_w, rs1_add_w, DEC_CP_q[14:0]}
  // Probe on {EXE_CP_q_3, EXE_CP_q[24:15], EXE_CP_q_2, EXE_CP_q[11:0]}
  // Probe on {WB_CP_q[31:12], rd_add_o, WB_CP_q[6:0]}
  Comparator #(.width(5)) comparator_1 (.a(rs2_add_w), .b(rd_add_o), .eq(comparator_1_eq));  // open: gt, lt
  Comparator #(.width(5)) comparator_2 (.a(rd_add_o), .b(rs1_add_w), .eq(comparator_2_eq));  // open: gt, lt
  Comparator #(.width(5)) comparator_3 (.a(rd_add_o), .b({5{1'b0}}), .eq(comparator_3_eq));  // open: gt, lt
  Register #(.width(32)) DEC_CP (
    .D(instruction_i), .en(not_1_out), .clk(clk_i),
    .Q({DEC_CP_q[31:25], rs2_add_w, rs1_add_w, DEC_CP_q[14:0]}), .clr(rst_i));
  Register #(.width(32)) EXE_CP (
    .D(multiplexer_1_out), .en(1'b1), .clk(clk_i),
    .Q({EXE_CP_q_3, EXE_CP_q[24:15], EXE_CP_q_2, EXE_CP_q[11:0]}), .clr(rst_i));
  Register #(.width(32)) MEM_CP (
    .D({EXE_CP_q_3, EXE_CP_q[24:15], EXE_CP_q_2, EXE_CP_q[11:0]}), .en(1'b1), .clk(clk_i), .Q(MEM_CP_q),
    .clr(rst_i));
  Register #(.width(32)) WB_CP (
    .D(MEM_CP_q), .en(1'b1), .clk(clk_i), .Q({WB_CP_q[31:12], rd_add_o, WB_CP_q[6:0]}), .clr(rst_i));
  Multiplexer #(.width(32)) multiplexer_1 (
    .in0({DEC_CP_q[31:25], rs2_add_w, rs1_add_w, DEC_CP_q[14:0]}), .in1(32'h13), .out(multiplexer_1_out),
    .sel(stall_o));
  or or_1 (or_1_out, comparator_1_eq, comparator_2_eq);
  // Probe on rs1_add_w
  // Probe on rs2_add_w
  and and_1 (stall_o, or_1_out, comparator_3_eq);
  PLA #(.in_width(3), .out_width(4), .\table ("000 0001 # add\n100 1000 # xor\n110 0111 # or\n111 0110 # and\n001 0011 # ssl\n101 0000")) R_Type_func (
    .in(EXE_CP_q_2), .out(R_Type_func_out));
  // Probe on rd_add_o
  Comparator #(.width(5)) comparator_4 (.a(5'b01100), .b(DEC_CP_q[6:2]), .eq(comparator_4_eq));  // open: gt, lt
  Comparator #(.width(5)) comparator_5 (.a(5'b00100), .b(DEC_CP_q[6:2]), .eq(comparator_5_eq));  // open: gt, lt
  Comparator #(.width(5)) comparator_6 (.a(5'b01101), .b(DEC_CP_q[6:2]), .eq(comparator_6_eq));  // open: gt, lt
  Multiplexer #(.width(3)) multiplexer_2 (
    .in0(priority_encoder_1_out), .in1(3'b001), .out(multiplexer_2_out), .sel(stall_o));
  Priority_Encoder priority_encoder_1 (
    .in0(comparator_4_eq), .in1(comparator_5_eq), .in2(comparator_6_eq), .out(priority_encoder_1_out),
    .en_in(1'b1));  // open: in3, in4, in5, in6, in7, gs, en_out
  Register #(.width(3)) EXE_OP (.D(multiplexer_2_out), .en(1'b1), .clk(clk_i), .Q(EXE_OP_q), .clr(rst_i));
  Register #(.width(3)) MEM_OP (.D(EXE_OP_q), .en(1'b1), .clk(clk_i), .Q(MEM_OP_q), .clr(rst_i));
  Register #(.width(3)) WB_OP (.D(MEM_OP_q), .en(1'b1), .clk(clk_i), .Q(WB_OP_q), .clr(rst_i));
  Multiplexer #(.select(3), .width(2)) multiplexer_3 (
    .in0(2'b00), .in1(2'b00), .in2(2'b01), .out(imm_gen_sel_o), .sel(priority_encoder_1_out));  // open: in3, in4, in5, in6, in7
  Multiplexer #(.select(3)) multiplexer_4 (
    .in0(1'b0), .in1(1'b1), .in2(1'b0), .out(alu_src2_o), .sel(priority_encoder_1_out));  // open: in3, in4, in5, in6, in7
  Multiplexer #(.select(3)) multiplexer_5 (
    .in0(1'b0), .in1(1'b0), .in2(1'b1), .out(alu_src1_o), .sel(priority_encoder_1_out));  // open: in3, in4, in5, in6, in7
  Multiplexer #(.select(3)) multiplexer_6 (
    .in0(1'b0), .in1(1'b0), .in2(1'b0), .out(mem_we_o), .sel(MEM_OP_q));  // open: in3, in4, in5, in6, in7
  Multiplexer #(.select(3)) multiplexer_7 (
    .in0(1'b1), .in1(1'b1), .in2(1'b1), .out(wb_sel_o), .sel(WB_OP_q));  // open: in3, in4, in5, in6, in7
  Multiplexer #(.select(3)) multiplexer_8 (
    .in0(1'b1), .in1(1'b1), .in2(1'b1), .out(reg_write_o), .sel(WB_OP_q));  // open: in3, in4, in5, in6, in7
  Multiplexer #(.select(3), .width(4)) multiplexer_9 (
    .in0(R_Type_func_out), .in1(R_Type_func_out), .in2(4'b1011), .out(alu_control_o), .sel(EXE_OP_q));  // open: in3, in4, in5, in6, in7

  // Other names for the same wires on the sheet: rd_add_w[4:0] = rd_add_o; stall_w = stall_o

  // Notes on the sheet:
  //   func_3
  //   func_7
  //   opcode
  //   R_TYPE
  //   I_TYPE
  //   U_TYPE
  //   R_TYPE
  //   R_TYPE
endmodule

module pipeline_5stages (
  input  clk_i,
  input  rst_i
);

  wire control_path_1_alu_src1_o, control_path_1_alu_src2_o, control_path_1_mem_we_o,
       control_path_1_reg_write_o, control_path_1_stall_o, control_path_1_wb_sel_o, data_path_1_it_o,
       data_path_1_zero_o;
  wire [1:0] control_path_1_imm_gen_sel_o;
  wire [3:0] control_path_1_alu_control_o;
  wire [4:0] control_path_1_rd_add_o;
  wire [31:0] data_path_1_instruction_o;

  data_path data_path_1 (
    .alu_control_i(control_path_1_alu_control_o), .alu_src1_i(control_path_1_alu_src1_o),
    .mem_we_i(control_path_1_mem_we_o), .stall_i(control_path_1_stall_o), .wb_sel_i(control_path_1_wb_sel_o),
    .rd_add_i(control_path_1_rd_add_o), .reg_write_i(control_path_1_reg_write_o),
    .imm_gen_sel_i(control_path_1_imm_gen_sel_o), .alu_src2_i(control_path_1_alu_src2_o), .clk_i(clk_i),
    .rst_i(rst_i), .instruction_o(data_path_1_instruction_o), .zero_o(data_path_1_zero_o),
    .it_o(data_path_1_it_o));
  control_path control_path_1 (
    .instruction_i(data_path_1_instruction_o), .clk_i(clk_i), .rst_i(rst_i), .alu_zero_i(data_path_1_zero_o),
    .alu_lt_i(data_path_1_it_o), .imm_gen_sel_o(control_path_1_imm_gen_sel_o),
    .alu_src2_o(control_path_1_alu_src2_o), .alu_src1_o(control_path_1_alu_src1_o),
    .alu_control_o(control_path_1_alu_control_o), .mem_we_o(control_path_1_mem_we_o),
    .rd_add_o(control_path_1_rd_add_o), .wb_sel_o(control_path_1_wb_sel_o), .stall_o(control_path_1_stall_o),
    .reg_write_o(control_path_1_reg_write_o));
endmodule

module instruction_memory (
  input  [7:0] add_i,
  output [31:0] data_o
);

  ROM #(.addrWidth(6), .dataWidth(32)) rom_1 (.addr(add_i[7:2]), .data(data_o));

  // Notes on the sheet:
  //   contents of rom_1 (hex, n*v repeats v):
  //   293 313 393 13 22e293 336313 43e393 13 528e33 630eb3 738f33 9*13
endmodule
